# Fritzing sketch DS18B20 (saved by Fritzing 0.9.2b)
breadboards: 1

parts:
  part = DS18B20 1-Wire Temperature Sensor [part_number=DS18B20]
  Raspberry_Pi1 = Raspberry Pi 2

nets:
  GND: part.GND, Raspberry_Pi1.GND
  N1: part.DQ, Raspberry_Pi1.GPIO4
  VDD: part.VDD, Raspberry_Pi1.3v3
